# Fritzing sketch Photobioreactor (saved by Fritzing 0.9.9b)
circuit board: 5.22887cm x 6.85274cm
breadboards: 1

parts:
  Q1 = Basic FET N-Channel [package="TO220 [THT]"]
  Q2 = Basic FET N-Channel [package="TO220 [THT]"]
  J1 = female pin header, 4 pins [form="♀ (female)"]
  J3 = Camdenboss CTB0158-2 [part_number=CTB0158-2 package=THT]
  J4 = Camdenboss CTB0158-2 [part_number=CTB0158-2 package=THT]
  J5 = Camdenboss CTB0158-2 [part_number=CTB0158-2 package=THT]
  J1_2 = Camdenboss CTB0158-2 [part_number=CTB0158-2 package=THT]
  J2 = Camdenboss CTB0158-2 [part_number=CTB0158-2 package=THT]
  Part1 = Adafruit HUZZAH32 ESP32 Feather [part_number="Adafruit #3405"]
  R4 = Resistor [tolerance=±5% resistance=10k package="2010 [SMD]"]
  R3 = Resistor [tolerance=±5% resistance=10k package="1206 [SMD]"]
  R1 = Resistor [tolerance=±5% resistance=10k package="1206 [SMD]"]
  R2 = Resistor [tolerance=±5% resistance=10k package="1206 [SMD]"]

nets:
  N1: Q1.gate, Part1.IO13_A12, R3.Pin_1
  N2: Q1.drain, J4.pin2
  N3: Q1.source, Q2.source, J1.pin4, J5.pin2, Part1.GND, R4.Pin_0, R3.Pin_0, R1.Pin_1, R2.Pin_0
  N4: Q2.gate, Part1.A1_DAC1, R4.Pin_1
  N5: Q2.drain, J3.pin2
  N6: J1.pin1, Part1.VBUS
  N7: J1.pin2, Part1.IO12_A11
  N8: J1.pin3, Part1.IO27_A10
  N9: J3.pin1, J4.pin1, J5.pin1
  N10: J1_2.pin1, Part1.IO32_A7, R2.Pin_1
  N11: J1_2.pin2, J2.pin1, Part1.3.3V
  N12: J2.pin2, Part1.A2_I34, R1.Pin_0

notes:
  [write your note here
  Power Supply
  LED
  Peristaltic
  Thermistor
  LDR
  Relay Air pump
